// Logisim project Trabalho.circ as structural Verilog: 14 circuits, main circuit Cronômetro Digital
module \Cronômetro_Digital  (
);

  wire _0_out, A0, A1, A2, A3, A4, A5, B0, B1, B2, B3, B4, B5, C0, C1, C2, C3, C4, C5, Clk, clock_1_out,
       \COMEÇAR , contador_0_a_999999ms_1_s0, contador_0_a_999999ms_1_s1, contador_0_a_999999ms_1_s2,
       contador_0_a_999999ms_1_s3, contador_0_a_999999ms_2_s0, contador_0_a_999999ms_2_s1,
       contador_0_a_999999ms_2_s2, contador_0_a_999999ms_2_s3, contador_0_a_999999ms_2_saida,
       contador_0_a_999999ms_3_s0, contador_0_a_999999ms_3_s1, contador_0_a_999999ms_3_s2,
       contador_0_a_999999ms_3_s3, contador_0_a_999999ms_3_saida, contador_0_a_999999ms_4_s0,
       contador_0_a_999999ms_4_s1, contador_0_a_999999ms_4_s2, contador_0_a_999999ms_4_s3,
       contador_0_a_999999ms_4_saida, contador_0_a_999999ms_5_s0, contador_0_a_999999ms_5_s1,
       contador_0_a_999999ms_5_s2, contador_0_a_999999ms_5_s3, contador_0_a_999999ms_5_saida,
       contador_0_a_999999ms_6_s0, contador_0_a_999999ms_6_s1, contador_0_a_999999ms_6_s2,
       contador_0_a_999999ms_6_s3, contador_0_a_999999ms_6_saida, CTR0, CTR1, CTR2, CTR3, CTR4, CTR5, D0, D1,
       D2, D3, D4, D5, DA, DB, DC, DD, DE, DF, DG, E0, E1, E2, E3, E4, E5, F0, F1, F2, F3, F4, F5, G0, G1,
       G2, G3, G4, G5, PAR, PARAR, Str, ZER, ZERAR;

  _7_Segment_Display u_7_segment_display_1 (.g(DG), .f(DF), .a(DA), .b(DB), .e(DE), .d(DD), .c(DC));  // open: dp
  Contador_0_a_999999ms contador_0_a_999999ms_1 (
    .S0(contador_0_a_999999ms_1_s0), .S1(contador_0_a_999999ms_1_s1), .S2(contador_0_a_999999ms_1_s2),
    .S3(contador_0_a_999999ms_1_s3), .ENTRADA(contador_0_a_999999ms_2_saida), .Clock(Clk), .PARAR(PAR),
    .ZERAR(ZER));  // open: SAIDA
  \Conversor_Binário  \conversor_binário_1  (
    .S0(contador_0_a_999999ms_1_s0), .S1(contador_0_a_999999ms_1_s1), .S2(contador_0_a_999999ms_1_s2),
    .S3(contador_0_a_999999ms_1_s3), ._0(CTR5), .A(A5), .B(B5), .C(C5), .D(D5), .E(E5), .F(F5), .G(G5));
  _7_Segment_Display u_7_segment_display_2 (.g(G5), .f(F5), .a(A5), .b(B5), .e(E5), .d(D5), .c(C5));  // open: dp
  \Botão_COMEÇAR  \botão_começar_1  (.ENTRADA(\COMEÇAR ), .S(Str));
  \Botão_PARAR  \botão_parar_1  (.ENTRADA(PARAR), .Start(Str), .S(PAR));
  _7_Segment_Display u_7_segment_display_3 (.g(G4), .f(F4), .a(A4), .b(B4), .e(E4), .d(D4), .c(C4));  // open: dp
  Contador_0_a_999999ms contador_0_a_999999ms_2 (
    .S0(contador_0_a_999999ms_2_s0), .S1(contador_0_a_999999ms_2_s1), .S2(contador_0_a_999999ms_2_s2),
    .S3(contador_0_a_999999ms_2_s3), .ENTRADA(contador_0_a_999999ms_3_saida), .Clock(Clk), .PARAR(PAR),
    .ZERAR(ZER), .SAIDA(contador_0_a_999999ms_2_saida));
  \Conversor_Binário  \conversor_binário_2  (
    .S0(contador_0_a_999999ms_2_s0), .S1(contador_0_a_999999ms_2_s1), .S2(contador_0_a_999999ms_2_s2),
    .S3(contador_0_a_999999ms_2_s3), ._0(CTR4), .A(A4), .B(B4), .C(C4), .D(D4), .E(E4), .F(F4), .G(G4));
  _7_Segment_Display u_7_segment_display_4 (.g(G3), .f(F3), .a(A3), .b(B3), .e(E3), .d(D3), .c(C3));  // open: dp
  \Botão_ZERAR  \botão_zerar_1  (.ZERAR(ZERAR), .\COMEÇAR (Str), .S(ZER));
  Contador_0_a_999999ms contador_0_a_999999ms_3 (
    .S0(contador_0_a_999999ms_3_s0), .S1(contador_0_a_999999ms_3_s1), .S2(contador_0_a_999999ms_3_s2),
    .S3(contador_0_a_999999ms_3_s3), .ENTRADA(contador_0_a_999999ms_4_saida), .Clock(Clk), .PARAR(PAR),
    .ZERAR(ZER), .SAIDA(contador_0_a_999999ms_3_saida));
  _7_Segment_Display u_7_segment_display_5 (.g(G2), .f(F2), .a(A2), .b(B2), .e(E2), .d(D2), .c(C2));  // open: dp
  and _0 (_0_out, CTR0, CTR1, CTR2, CTR3, CTR4, CTR5);
  \Conversor_Binário  \conversor_binário_3  (
    .S0(contador_0_a_999999ms_3_s0), .S1(contador_0_a_999999ms_3_s1), .S2(contador_0_a_999999ms_3_s2),
    .S3(contador_0_a_999999ms_3_s3), ._0(CTR3), .A(A3), .B(B3), .C(C3), .D(D3), .E(E3), .F(F3), .G(G3));
  _7_Segment_Display u_7_segment_display_6 (.g(G1), .f(F1), .a(A1), .b(B1), .e(E1), .d(D1), .c(C1));  // open: dp
  Controlador_do_Display controlador_do_display_1 (
    ._0(_0_out), .PARAR(PAR), .A(DA), .B(DB), .C(DC), .D(DD), .E(DE), .F(DF), .G(DG));
  Contador_0_a_999999ms contador_0_a_999999ms_4 (
    .S0(contador_0_a_999999ms_4_s0), .S1(contador_0_a_999999ms_4_s1), .S2(contador_0_a_999999ms_4_s2),
    .S3(contador_0_a_999999ms_4_s3), .ENTRADA(contador_0_a_999999ms_5_saida), .Clock(Clk), .PARAR(PAR),
    .ZERAR(ZER), .SAIDA(contador_0_a_999999ms_4_saida));
  \Conversor_Binário  \conversor_binário_4  (
    .S0(contador_0_a_999999ms_4_s0), .S1(contador_0_a_999999ms_4_s1), .S2(contador_0_a_999999ms_4_s2),
    .S3(contador_0_a_999999ms_4_s3), ._0(CTR2), .A(A2), .B(B2), .C(C2), .D(D2), .E(E2), .F(F2), .G(G2));
  _7_Segment_Display u_7_segment_display_7 (.g(G0), .f(F0), .a(A0), .b(B0), .e(E0), .d(D0), .c(C0));  // open: dp
  Clock clock_1 (.out(clock_1_out));
  Contador_0_a_999999ms contador_0_a_999999ms_5 (
    .S0(contador_0_a_999999ms_5_s0), .S1(contador_0_a_999999ms_5_s1), .S2(contador_0_a_999999ms_5_s2),
    .S3(contador_0_a_999999ms_5_s3), .ENTRADA(contador_0_a_999999ms_6_saida), .Clock(Clk), .PARAR(PAR),
    .ZERAR(ZER), .SAIDA(contador_0_a_999999ms_5_saida));
  \Conversor_Binário  \conversor_binário_5  (
    .S0(contador_0_a_999999ms_5_s0), .S1(contador_0_a_999999ms_5_s1), .S2(contador_0_a_999999ms_5_s2),
    .S3(contador_0_a_999999ms_5_s3), ._0(CTR1), .A(A1), .B(B1), .C(C1), .D(D1), .E(E1), .F(F1), .G(G1));
  Button u_ZERAR (.out(ZERAR));
  Button u_PARAR (.out(PARAR));
  Button \u_COMEÇAR  (.out(\COMEÇAR ));
  and and_1 (Clk, Str, clock_1_out);
  Contador_0_a_999999ms contador_0_a_999999ms_6 (
    .S0(contador_0_a_999999ms_6_s0), .S1(contador_0_a_999999ms_6_s1), .S2(contador_0_a_999999ms_6_s2),
    .S3(contador_0_a_999999ms_6_s3), .ENTRADA(1'b1), .Clock(Clk), .PARAR(PAR), .ZERAR(ZER),
    .SAIDA(contador_0_a_999999ms_6_saida));
  \Conversor_Binário  \conversor_binário_6  (
    .S0(contador_0_a_999999ms_6_s0), .S1(contador_0_a_999999ms_6_s1), .S2(contador_0_a_999999ms_6_s2),
    .S3(contador_0_a_999999ms_6_s3), ._0(CTR0), .A(A0), .B(B0), .C(C0), .D(D0), .E(E0), .F(F0), .G(G0));

  // Notes on the sheet:
  //   DISPALY
  //   Cont. 5
  //   Conv. 5
  //   COMEÇAR
  //   PARAR
  //   Cont. 4
  //   Conv. 4
  //   ZERAR
  //   CRONÔMETRO
  //   Cont. 3
  //   Conv. 3
  //   CONTROLADOR DISPLAY
  //   CONTADOR E CONVERSOR
  //   Cont. 2
  //   Conv. 2
  //   Cont. 1
  //   Conv. 1
  //   MENU
  //   COMEÇAR/CLICK
  //   SAIDA
  //   ENTARADA
  //   ENTRADA
  //   Cont. 0
  //   Conv. 0
endmodule

module A (
  input  Q0,
  input  Q1,
  input  Q2,
  input  Q3,
  output A
);

  wire and_1_out, and_2_out, and_3_out, and_4_out;

  and and_1 (and_1_out, ~Q3, Q1);  // AND_Gate
  and and_2 (and_2_out, ~Q3, Q2, Q0);  // AND_Gate
  and and_3 (and_3_out, ~Q2, ~Q1, ~Q0);  // AND_Gate
  and and_4 (and_4_out, Q3, ~Q2, ~Q1);  // AND_Gate
  or or_1 (A, and_1_out, and_2_out, and_3_out, and_4_out);
endmodule

module B (
  input  Q0,
  input  Q1,
  input  Q2,
  input  Q3,
  output B
);

  wire and_1_out, and_2_out, and_3_out, and_4_out;

  and and_1 (and_1_out, ~Q3, ~Q2);  // AND_Gate
  and and_2 (and_2_out, ~Q2, ~Q1);  // AND_Gate
  and and_3 (and_3_out, ~Q3, ~Q1, ~Q0);  // AND_Gate
  and and_4 (and_4_out, ~Q3, Q1, Q0);  // AND_Gate
  or or_1 (B, and_1_out, and_2_out, and_3_out, and_4_out);
endmodule

module C (
  input  Q0,
  input  Q1,
  input  Q2,
  input  Q3,
  output C
);

  wire and_1_out, and_2_out, and_3_out;

  and and_1 (and_1_out, ~Q2, ~Q1);  // AND_Gate
  and and_2 (and_2_out, ~Q3, Q2);  // AND_Gate
  and and_3 (and_3_out, ~Q3, ~Q2, Q0);  // AND_Gate
  or or_1 (C, and_1_out, and_2_out, and_3_out);
endmodule

module D (
  input  Q0,
  input  Q1,
  input  Q2,
  input  Q3,
  output D
);

  wire and_1_out, and_2_out, and_3_out, and_4_out;

  and and_1 (and_1_out, ~Q3, ~Q2, Q1);  // AND_Gate
  and and_2 (and_2_out, ~Q3, Q1, ~Q0);  // AND_Gate
  and and_3 (and_3_out, ~Q2, ~Q1, ~Q0);  // AND_Gate
  and and_4 (and_4_out, ~Q3, Q2, ~Q1, Q0);  // AND_Gate
  or or_1 (D, and_1_out, and_2_out, and_3_out, and_4_out);
endmodule

module E (
  input  Q0,
  input  Q1,
  input  Q2,
  input  Q3,
  output E
);

  wire and_1_out, and_2_out;

  and and_1 (and_1_out, ~Q2, ~Q1, ~Q0);  // AND_Gate
  and and_2 (and_2_out, ~Q3, Q1, ~Q0);  // AND_Gate
  or or_1 (E, and_1_out, and_2_out);
endmodule

module F (
  input  Q0,
  input  Q1,
  input  Q2,
  input  Q3,
  output F
);

  wire and_1_out, and_2_out, and_3_out, and_4_out;

  and and_1 (and_1_out, ~Q3, ~Q1, ~Q0);  // AND_Gate
  and and_2 (and_2_out, ~Q3, Q2, ~Q1);  // AND_Gate
  and and_3 (and_3_out, ~Q3, Q2, ~Q0);  // AND_Gate
  and and_4 (and_4_out, Q3, ~Q2, ~Q1);  // AND_Gate
  or or_1 (F, and_1_out, and_2_out, and_3_out, and_4_out);
endmodule

module G (
  input  Q0,
  input  Q1,
  input  Q2,
  input  Q3,
  output G
);

  wire and_1_out, and_2_out, and_3_out, and_4_out;

  and and_1 (and_1_out, ~Q3, ~Q2, Q1);  // AND_Gate
  and and_2 (and_2_out, ~Q3, Q2, ~Q1);  // AND_Gate
  and and_3 (and_3_out, ~Q3, Q2, ~Q0);  // AND_Gate
  and and_4 (and_4_out, Q3, ~Q2, ~Q1);  // AND_Gate
  or or_1 (G, and_1_out, and_2_out, and_3_out, and_4_out);
endmodule

module Contador_0_a_999999ms (
  input  ENTRADA,
  input  Clock,
  input  PARAR,
  input  ZERAR,
  output S0,
  output S1,
  output S2,
  output S3,
  output SAIDA
);

  wire and_1_out, and_2_out, and_3_out, and_4_out, buffer_1_out, j_k_ff_1_qn, j_k_ff_3_qn, or_1_out;

  J_K_Flip_Flop j_k_ff_1 (
    .J(ENTRADA), .clk(Clock), .K(ENTRADA), .Q(S0), .Qn(j_k_ff_1_qn), .en(PARAR), .reset(buffer_1_out));  // open: preset
  and and_1 (and_1_out, ENTRADA, S0);
  J_K_Flip_Flop j_k_ff_2 (
    .J(and_1_out), .clk(Clock), .K(and_1_out), .Q(S1), .en(PARAR), .reset(buffer_1_out));  // open: Qn, preset
  and and_2 (and_2_out, and_1_out, S1);
  J_K_Flip_Flop j_k_ff_3 (
    .J(and_2_out), .clk(Clock), .K(and_2_out), .Q(S2), .Qn(j_k_ff_3_qn), .en(PARAR), .reset(buffer_1_out));  // open: preset
  and and_3 (and_3_out, and_2_out, S2);
  J_K_Flip_Flop j_k_ff_4 (
    .J(and_3_out), .clk(Clock), .K(and_3_out), .Q(S3), .en(PARAR), .reset(buffer_1_out));  // open: Qn, preset
  and and_4 (and_4_out, S3, j_k_ff_3_qn, S1, j_k_ff_1_qn);
  and and_5 (SAIDA, and_1_out, S3);
  buf buffer_1 (buffer_1_out, or_1_out);
  or or_1 (or_1_out, and_4_out, ZERAR);
endmodule

module \Conversor_Binário  (
  input  S0,
  input  S1,
  input  S2,
  input  S3,
  output A,
  output B,
  output _0,
  output C,
  output D,
  output E,
  output F,
  output G
);

  A a_1 (.Q0(S0), .Q1(S1), .Q2(S2), .Q3(S3), .A(A));
  B b_1 (.Q0(S0), .Q1(S1), .Q2(S2), .Q3(S3), .B(B));
  C c_1 (.Q0(S0), .Q1(S1), .Q2(S2), .Q3(S3), .C(C));
  D d_1 (.Q0(S0), .Q1(S1), .Q2(S2), .Q3(S3), .D(D));
  E e_1 (.Q0(S0), .Q1(S1), .Q2(S2), .Q3(S3), .E(E));
  F f_1 (.Q0(S0), .Q1(S1), .Q2(S2), .Q3(S3), .F(F));
  G g_1 (.Q0(S0), .Q1(S1), .Q2(S2), .Q3(S3), .G(G));
  and and_1 (_0, ~G, F, E, D, C, B, A);  // AND_Gate
endmodule

module Controlador_do_Display (
  input  _0,
  input  PARAR,
  output A,
  output B,
  output C,
  output D,
  output E,
  output F,
  output G
);

  wire and_1_out;

  and and_1 (and_1_out, ~PARAR, ~_0);  // AND_Gate
  and and_2 (B, ~_0, PARAR);  // AND_Gate
  or or_1 (A, and_1_out, B);
  or or_2 (G, and_1_out, B);
  or or_3 (D, _0, and_1_out);
  or or_4 (E, _0, and_1_out, B);
  or or_5 (F, _0, and_1_out, B);

  assign C = B;
endmodule

module \Botão_PARAR  (
  input  Start,
  input  ENTRADA,
  output S
);

  wire and_1_out, j_k_ff_1_q;

  and and_1 (and_1_out, Start, ENTRADA);
  J_K_Flip_Flop j_k_ff_1 (
    .J(and_1_out), .clk(and_1_out), .K(and_1_out), .Q(j_k_ff_1_q));  // open: Qn, preset, en, reset
  not not_1 (S, j_k_ff_1_q);
endmodule

module \Botão_COMEÇAR  (
  input  ENTRADA,
  output S
);

  J_K_Flip_Flop j_k_ff_1 (.J(ENTRADA), .clk(ENTRADA), .K(ENTRADA), .Q(S));  // open: Qn, preset, en, reset
endmodule

module \Botão_ZERAR  (
  input  \COMEÇAR ,
  input  ZERAR,
  output S
);

  wire and_1_out;

  and and_1 (and_1_out, \COMEÇAR , ZERAR);
  or or_1 (S, ~\COMEÇAR , and_1_out);  // OR_Gate
endmodule
